# Fritzing sketch RPi-Jukebox-RFID (saved by Fritzing 0.9.3b)
breadboards: 1

parts:
  Raspberry_Pi_1 = Raspberry Pi 3 [part_number=RPI-3-V1.2]
  S1 = SWITCH-MOMENTARY-2 [package=tactile-pth-12mm]
  S2 = SWITCH-MOMENTARY-2 [package=tactile-pth-12mm]
  S3 = SWITCH-MOMENTARY-2 [package=tactile-pth-12mm]
  S4 = SWITCH-MOMENTARY-2 [package=tactile-pth-12mm]
  S5 = SWITCH-MOMENTARY-2 [package=tactile-pth-12mm]
  S6 = SWITCH-MOMENTARY-2 [package=tactile-pth-12mm]

nets:
  N1: Raspberry_Pi_1.GPIO3, S1.2
  N2: Raspberry_Pi_1.GND, S3.2, S4.2, S5.2, S6.2
  N3: Raspberry_Pi_1.GPIO19, S2.2

notes:
  Shutdown and Switch on
  (to shut down hold for 2 sec)
  Volume Down
  Volume Up
  Play/Pause/Halt
  Next
  Previous

// code stored in the sketch: RPi-Jukebox-RFID.ino
https://github.com/MiczFlor/RPi-Jukebox-RFID/wiki/img/GPIO-pin-numbering.png


How to connect the buttons
Here is how to connect the buttons:
Volume Down GPIO19 (PIN35) and GND (PIN39)
Volume Up GPIO16 (PIN36) and GND (PIN34)
Play/Pause/Halt (or how you call it) GPIO21 (PIN40) and GND (PIN25)
Next GPIO26 (PIN37) and GND (PIN30)
Previous GPIO20 (PIN38) and GND (PIN20)
Shutdown (you need to hold button for 2 secs for shutdown) GPIO3 (PIN5) and GND (PIN6)
!!! IMPORTANT Only when using the above listed pins for wiring your shutdown pin you will be able to power-up the Raspberry PI from firmware halt. !!!
Circuit example(s) for the button wiring
You will be using push buttons, which are essentially the same as arcade buttons, meaning: when you press them down, they are ON, when you let go, the are OFF. So skipping a track is tapping a button once, changing the volume, each tap changes it a bit. The updated GPIO from pullrequest #306 added the option to hold down the volume buttons and change every 0.3 seconds the volume according to the configured volume steps.
